# Fritzing sketch prototype (saved by Fritzing 0.9.3b)
breadboards: 1

parts:
  S1 = Pushbutton [package="[THT]"]
  S2 = Pushbutton [package="[THT]"]
  U2 = 7-SEGMENT-4DIGIT [package=7-segment-4digit-5641]
  U3 = atmega8 [package=dip]
  R1 = Resistor [tolerance=±5% resistance=10k package=THT]
  R2 = Resistor [tolerance=±5% resistance=10k package=THT]
  Q1 = NPN-Transistor [package="TO92 [THT]"]
  R3 = Resistor [tolerance=±5% resistance=220 package=THT]
  Q2 = NPN-Transistor [package="TO92 [THT]"]
  R4 = Resistor [tolerance=±5% resistance=220 package=THT]
  Q3 = NPN-Transistor [package="TO92 [THT]"]
  Q4 = NPN-Transistor [package="TO92 [THT]"]
  R5 = Resistor [tolerance=±5% resistance=220 package=THT]
  R6 = Resistor [tolerance=±5% resistance=220 package=THT]
  R7 = Resistor [tolerance=±5% resistance=220 package=THT]
  R8 = Resistor [tolerance=±5% resistance=220 package=THT]
  R9 = Resistor [tolerance=±5% resistance=220 package=THT]
  R10 = Resistor [tolerance=±5% resistance=220 package=THT]
  R11 = Resistor [tolerance=±5% resistance=220 package=THT]
  R12 = Resistor [tolerance=±5% resistance=220 package=THT]
  R13 = Resistor [tolerance=±5% resistance=220 package=THT]
  R14 = Resistor [tolerance=±5% resistance=220 package=THT]
  S3 = Toggle Switch [package=THT]
  VCC1 = Battery

nets:
  N1: S1.Pin_1, S1.Pin_2, R1.Pin_0
  N2: S1.Pin_3, S1.Pin_4, S2.Pin_1, S2.Pin_2, U3.GND#7, Q1.C, Q2.C, Q3.C, Q4.C, VCC1.-
  N3: S2.Pin_3, S2.Pin_4, R2.Pin_1
  N4: U2.DIG2, Q3.B
  N5: U2.DIG3, Q2.B
  N6: U2.DIG4, Q1.B
  N7: U2.A, R9.Pin_1
  N8: U2.B, R8.Pin_1
  N9: U2.C, R7.Pin_1
  N10: U2.D, R10.Pin_0
  N11: U2.E, R11.Pin_0
  N12: U2.F, R12.Pin_0
  N13: U2.G, R13.Pin_0
  N14: U2.DP, R14.Pin_0
  N15: U2.DIG1, Q4.B
  N16: U3.D0_(RX), R14.Pin_1
  N17: U3.D1_(TX), R13.Pin_1
  N18: U3.D2, R12.Pin_1
  N19: U3.D3_(PWM), R11.Pin_1
  N20: U3.D4, R10.Pin_1
  N21: U3.VCC, S3.L2
  N22: U3.D5_(PWM), R7.Pin_0
  N23: U3.D6_(PWM), R8.Pin_0
  N24: U3.D7, R9.Pin_0
  N25: U3.D8, R3.Pin_0
  N26: U3.D9_(PWM), R4.Pin_0
  N27: U3.D10_(PWM), R5.Pin_0
  N28: U3.D11_(PWM), R6.Pin_0
  N29: U3.D12, R2.Pin_0
  N30: U3.D13, R1.Pin_1
  N31: Q1.E, R3.Pin_1
  N32: Q2.E, R4.Pin_1
  N33: Q3.E, R5.Pin_1
  N34: Q4.E, R6.Pin_1

custom parts:
  7-SEGMENT-4DIGIT: if you need make parts, send me e-mail and write. Price 1 part=0.9 WMZ (http://www.wmtransfer.com/) ~ 0.9 Euro
  atmega8: Atmel ATmega168 microcontroller. The hardware hacker favorite.
